// Logisim project Basic Computer.circ as structural Verilog: 1 circuit, main circuit main
module main (
  input  in_1,
  input  in_2,
  input  in_3,
  input  in_4,
  input  in_5,
  input  in_6,
  input  [2:0] in_7,
  input  in_8,
  input  in_9,
  input  [2:0] in_10,
  input  in_11
);

  wire clock_1_out;
  wire [6:0] AR_q, bit_extender_1_out;
  wire [15:0] AC_q, adder_1_out, adder_2_out, and_1_out, bit_extender_2_out, DR_q, multiplexer_1_out,
       multiplexer_2_out, multiplier_1_out, or_1_out, ram_1_data, subtractor_1_out, TR_q;

  Clock clock_1 (.out(clock_1_out));
  Bit_Extender #(.in_width(16), .out_width(7)) bit_extender_1 (.in(multiplexer_2_out), .out(bit_extender_1_out));
  Register #(.width(7)) AR (.D(bit_extender_1_out), .en(in_5), .Q(AR_q), .clk(clock_1_out));  // open: clr
  Register #(.width(16)) DR (.D(multiplexer_2_out), .en(in_6), .Q(DR_q), .clk(clock_1_out));  // open: clr
  Register #(.width(16)) AC (.D(multiplexer_1_out), .en(in_8), .Q(AC_q), .clk(clock_1_out));  // open: clr
  Register #(.width(16)) TR (.D(multiplexer_2_out), .en(in_11), .Q(TR_q), .clk(clock_1_out));  // open: clr
  assign bit_extender_2_out = {{9{1'b0}}, AR_q};  // Bit_Extender bit_extender_2
  RAM #(.addrWidth(7), .dataWidth(16), .bus("separate")) ram_1 (
    .addr(AR_q), .din(multiplexer_2_out), .data(ram_1_data), .str(in_3), .sel(in_1), .clk(clock_1_out),
    .ld(in_2));  // open: clr
  Adder #(.width(16)) adder_1 (.a(DR_q), .b(AC_q), .out(adder_1_out));  // open: cin, cout
  Subtractor #(.width(16)) subtractor_1 (.a(DR_q), .b(AC_q), .out(subtractor_1_out));  // open: bin, bout
  Multiplier #(.width(16)) multiplier_1 (.a(DR_q), .b(AC_q), .out(multiplier_1_out));  // open: cin, cout
  Adder #(.width(16)) adder_2 (.a(DR_q), .b(16'h1), .out(adder_2_out));  // open: cin, cout
  assign or_1_out = DR_q | AC_q;  // OR_Gate or_1, 16 bits wide
  assign and_1_out = DR_q & AC_q;  // AND_Gate and_1, 16 bits wide
  Multiplexer #(.select(3), .width(16)) multiplexer_1 (
    .in1(DR_q), .in2(adder_1_out), .in3(subtractor_1_out), .in4(multiplier_1_out), .in5(adder_2_out),
    .in6(or_1_out), .in7(and_1_out), .out(multiplexer_1_out), .sel(in_10), .en(in_9));  // open: in0
  Multiplexer #(.select(3), .width(16)) multiplexer_2 (
    .in0(AC_q), .in1(DR_q), .in2(TR_q), .in3(bit_extender_2_out), .in4(ram_1_data), .out(multiplexer_2_out),
    .sel(in_7), .en(in_4));  // open: in5, in6, in7
endmodule
